// Logisim project Lab6.circ as structural Verilog: 28 circuits, main circuit main
module main (
  output [15:0] instr_count,
  output FET,
  output DEC,
  output EXE,
  output MEM,
  output WB,
  output PCU,
  output [3:0] icode,
  output [3:0] ifun,
  output [3:0] rA,
  output [3:0] rB,
  output [63:0] valC,
  output [11:0] valP,
  output HLT,
  output [63:0] valA,
  output [63:0] valB,
  output [63:0] rax,
  output [63:0] rcx,
  output [63:0] rdx,
  output [63:0] rbx,
  output [63:0] rsp,
  output [63:0] rbp,
  output [63:0] rsi,
  output [63:0] rdi,
  output [63:0] r8,
  output [63:0] r9,
  output [63:0] r10,
  output [63:0] r11,
  output [63:0] r12,
  output [63:0] r13,
  output [63:0] r14,
  output [63:0] valE,
  output [63:0] valM,
  output [11:0] PC
);

  wire clk_out, cond_1_cnd, memread_1_reade, memwrite_1_writee, setcc_1_set;
  wire [1:0] alu_fun_1_fn;
  wire [2:0] cc_1_code;
  wire [3:0] dste_1_dst_e, dstm_1_dst_m, srca_1_src_a, srcb_1_src_b;
  wire [11:0] memaddr_1_addrin;
  wire [63:0] alu_1_pa, alu_1_pb, alu_a_1_a, alu_b_1_b, memdata_1_datain;

  Clock clk (.out(clk_out));
  GlobalCounter globalcounter_1 (
    .clk(clk_out), .HLT(HLT), .instr_count(instr_count), .FET(FET), .DEC(DEC), .EXE(EXE), .MEM(MEM), .WB(WB),
    .PCU(PCU));
  FetchUnit fetchunit_1 (
    .PC(PC), .clk(clk_out), .en(FET), .icode(icode), .ifun(ifun), .rA(rA), .rB(rB), .valC(valC), .valP(valP),
    .HLT(HLT));
  MemAddr memaddr_1 (.icode(icode), .valE(valE), .valA(valA), .AddrIn(memaddr_1_addrin));
  dstE dste_1 (.icode(icode), .rB(rB), .WB(WB), .dst_E(dste_1_dst_e));
  dstM dstm_1 (.icode(icode), .rA(rA), .WB(WB), .dst_M(dstm_1_dst_m));
  srcA srca_1 (.icode(icode), .rA(rA), .src_A(srca_1_src_a));
  srcB srcb_1 (.icode(icode), .rB(rB), .src_B(srcb_1_src_b));
  ALU_A alu_a_1 (.valA(valA), .valC(valC), .icode(icode), .A(alu_a_1_a));
  ALU_B alu_b_1 (.valB(valB), .icode(icode), .B(alu_b_1_b));
  ALU_fun alu_fun_1 (.ifun(ifun), .icode(icode), .fn(alu_fun_1_fn));
  SetCC setcc_1 (.icode(icode), .set(setcc_1_set));
  MemWrite memwrite_1 (.icode(icode), .WriteE(memwrite_1_writee));
  MemRead memread_1 (.icode(icode), .ReadE(memread_1_reade));
  MemData memdata_1 (.icode(icode), .valA(valA), .valP(valP), .DataIn(memdata_1_datain));
  UpdateUnit updateunit_1 (
    .icode(icode), .Cnd(cond_1_cnd), .valP(valP), .valC(valC), .valM(valM), .PCU(PCU), .clk(clk_out), .PC(PC));
  ALU alu_1 (.A(alu_a_1_a), .B(alu_b_1_b), .fn(alu_fun_1_fn), .valE(valE), .pA(alu_1_pa), .pB(alu_1_pb));
  DataMemory datamemory_1 (
    .mwrite(memwrite_1_writee), .mread(memread_1_reade), .mAddress(memaddr_1_addrin),
    .mData(memdata_1_datain), .en(MEM), .clk(clk_out), .valM(valM));
  RegisterFile registerfile_1 (
    .valE(valE), .valM(valM), .dstE(dste_1_dst_e), .dstM(dstm_1_dst_m), .srcA(srca_1_src_a),
    .srcB(srcb_1_src_b), .clk(clk_out), .write_en(WB), .read_en(DEC), .valA(valA), .valB(valB),
    .val_rax(rax), .val_rcx(rcx), .val_rdx(rdx), .val_rbx(rbx), .val_rsp(rsp), .val_rbp(rbp), .val_rsi(rsi),
    .val_rdi(rdi), .val_r8(r8), .val_r9(r9), .val_r10(r10), .val_r11(r11), .val_r12(r12), .val_r13(r13),
    .val_r14(r14));
  CC cc_1 (.SetCC(setcc_1_set), .valE(valE), .A(alu_1_pa), .B(alu_1_pb), .clk(clk_out), .en(EXE), .code(cc_1_code));
  cond cond_1 (.code(cc_1_code), .ifun(ifun), .Cnd(cond_1_cnd));

  // Notes on the sheet:
  //   Fetch
  //   Decode
  //   Write Back
  //   Execute
  //   Memory
  //   PC Update
endmodule

module FetchUnit (
  input  [11:0] PC,
  input  clk,
  input  en,
  output [3:0] icode,
  output [3:0] ifun,
  output [3:0] rA,
  output [3:0] rB,
  output [63:0] valC,
  output [11:0] valP,
  output HLT
);

  wire need_regids_1_needregids, need_valc_1_needvalc;
  wire [7:0] instructionmemory_1_byte1, instructionmemory_1_byte2, instructionmemory_1_byte3,
       instructionmemory_1_byte4, instructionmemory_1_byte5, instructionmemory_1_byte6,
       instructionmemory_1_byte7, instructionmemory_1_byte8, instructionmemory_1_byte9;

  InstructionMemory instructionmemory_1 (
    .PC(PC), .clk(clk), .en(en), .Byte0({icode, ifun}), .Byte1(instructionmemory_1_byte1),
    .Byte2(instructionmemory_1_byte2), .Byte3(instructionmemory_1_byte3), .Byte4(instructionmemory_1_byte4),
    .Byte5(instructionmemory_1_byte5), .Byte6(instructionmemory_1_byte6), .Byte7(instructionmemory_1_byte7),
    .Byte8(instructionmemory_1_byte8), .Byte9(instructionmemory_1_byte9));
  Need_valC need_valc_1 (.icode(icode), .NeedValC(need_valc_1_needvalc));
  Need_Regids need_regids_1 (.icode(icode), .NeedRegids(need_regids_1_needregids));
  Align align_1 (
    .Byte1(instructionmemory_1_byte1), .Byte2(instructionmemory_1_byte2), .Byte3(instructionmemory_1_byte3),
    .Byte4(instructionmemory_1_byte4), .Byte5(instructionmemory_1_byte5), .Byte6(instructionmemory_1_byte6),
    .Byte7(instructionmemory_1_byte7), .Byte8(instructionmemory_1_byte8), .Byte9(instructionmemory_1_byte9),
    .NeedRegids(need_regids_1_needregids), .rA(rA), .rB(rB), .valC(valC));
  PC_Increment pc_increment_1 (
    .NeedValC(need_valc_1_needvalc), .NeedRegids(need_regids_1_needregids), .PC(PC), .valP(valP));
  Comparator #(.mode("unsigned"), .width(4)) comparator_1 (.a(icode), .b(4'b0000), .eq(HLT));  // open: gt, lt

  // Notes on the sheet:
  //   Split
endmodule

module InstructionMemory (
  input  [11:0] PC,
  input  clk,
  input  en,
  output [7:0] Byte0,
  output [7:0] Byte1,
  output [7:0] Byte2,
  output [7:0] Byte3,
  output [7:0] Byte4,
  output [7:0] Byte5,
  output [7:0] Byte6,
  output [7:0] Byte7,
  output [7:0] Byte8,
  output [7:0] Byte9
);

  wire counter_1_q, decoder_1_out0, decoder_1_out1, decoder_1_out2, decoder_1_out3, decoder_1_out4,
       decoder_1_out5, decoder_1_out6, decoder_1_out7, decoder_1_out8, decoder_1_out9, not_1_out, undriven;
  wire [3:0] counter_2_q;
  wire [7:0] rom_1_data;
  wire [11:0] adder_1_out;

  Counter #(.max('h1), .ongoal("stay"), .width(1)) counter_1 (
    .clr(undriven), .clk(clk), .Q(counter_1_q));  // open: load, up, count, D, carry
  Counter #(.max('h9), .width(4)) counter_2 (
    .clr(not_1_out), .count(counter_1_q), .clk(clk), .Q(counter_2_q));  // open: load, up, D, carry
  not not_1 (not_1_out, en);
  ROM #(.addrWidth(12)) rom_1 (.addr(adder_1_out), .data(rom_1_data));
  Adder #(.width(12)) adder_1 (.a(PC), .b({{8{1'b0}}, counter_2_q}), .out(adder_1_out));  // open: cin, cout
  Decoder #(.select(4)) decoder_1 (
    .out0(decoder_1_out0), .out1(decoder_1_out1), .out2(decoder_1_out2), .out3(decoder_1_out3),
    .out4(decoder_1_out4), .out5(decoder_1_out5), .out6(decoder_1_out6), .out7(decoder_1_out7),
    .out8(decoder_1_out8), .out9(decoder_1_out9), .sel(counter_2_q), .en(en));  // open: out10, out11, out12, out13, out14, out15
  Register register_1 (.D(rom_1_data), .en(decoder_1_out0), .clk(clk), .Q(Byte0));  // open: clr
  Register register_2 (.D(rom_1_data), .en(decoder_1_out1), .clk(clk), .Q(Byte1));  // open: clr
  Register register_3 (.D(rom_1_data), .en(decoder_1_out2), .clk(clk), .Q(Byte2));  // open: clr
  Register register_4 (.D(rom_1_data), .en(decoder_1_out3), .clk(clk), .Q(Byte3));  // open: clr
  Register register_5 (.D(rom_1_data), .en(decoder_1_out4), .clk(clk), .Q(Byte4));  // open: clr
  Register register_6 (.D(rom_1_data), .en(decoder_1_out5), .clk(clk), .Q(Byte5));  // open: clr
  Register register_7 (.D(rom_1_data), .en(decoder_1_out6), .clk(clk), .Q(Byte6));  // open: clr
  Register register_8 (.D(rom_1_data), .en(decoder_1_out7), .clk(clk), .Q(Byte7));  // open: clr
  Register register_9 (.D(rom_1_data), .en(decoder_1_out8), .clk(clk), .Q(Byte8));  // open: clr
  Register register_10 (.D(rom_1_data), .en(decoder_1_out9), .clk(clk), .Q(Byte9));  // open: clr

  // Notes on the sheet:
  //   don't want to increment counter until second clock tick
  //   contents of rom_1 (hex, n*v repeats v):
  //   30 f4 0 f 6*0 80 ec 8*0 9 7*0 8 7*0 7 7*0 6 7*0 5 7*0 4 7*0 3 7*0 2 7*0 1 7*0 1 7*0 2 7*0 3 7*0 4
  //   7*0 5 7*0 6 7*0 7 7*0 8 7*0 9 79*0 30 fc 3 7*0 30 f6 8*0 30 f7 8*0 10 20 68 61 c8 75 9d 1 6*0 30 f7
  //   8*0 20 79 61 c9 75 88 1 6*0 20 6*60 70 20 a 60 a0 60 a0 60 a0 60 a0 60 a0 60 a0 60 a0 50 30 14 7*0
  //   50 20 5c 7*0 60 23 30 f8 4 7*0 60 80 40 30 a4 7*0 30 fd 1 7*0 60 d7 70 22 1 6*0 30 fd 1 7*0 60 d6 70
  //   b 1 6*0 90
endmodule

module PC_Increment (
  input  NeedValC,
  input  NeedRegids,
  input  [11:0] PC,
  output [11:0] valP
);

  wire [11:0] adder_1_out, adder_2_out, multiplier_1_out;

  Multiplier #(.width(12)) multiplier_1 (
    .a({{11{1'b0}}, NeedValC}), .b(12'h8), .out(multiplier_1_out));  // open: cin, cout
  Adder #(.width(12)) adder_1 (.a(12'h1), .b({{11{1'b0}}, NeedRegids}), .out(adder_1_out));  // open: cin, cout
  Adder #(.width(12)) adder_2 (.a(multiplier_1_out), .b(adder_1_out), .out(adder_2_out));  // open: cin, cout
  Adder #(.width(12)) adder_3 (.a(adder_2_out), .b(PC), .out(valP));  // open: cin, cout
endmodule

module Need_valC (
  input  [3:0] icode,
  output NeedValC
);

  wire and_1_out, and_2_out, and_3_out, and_4_out, and_5_out;

  and and_1 (and_1_out, icode[0], icode[2], ~icode[1], ~icode[3]);  // AND_Gate
  and and_2 (and_2_out, ~icode[0], icode[2], ~icode[1], ~icode[3]);  // AND_Gate
  and and_3 (and_3_out, icode[0], ~icode[2], icode[1], ~icode[3]);  // AND_Gate
  and and_4 (and_4_out, icode[0], icode[2], icode[1], ~icode[3]);  // AND_Gate
  and and_5 (and_5_out, ~icode[0], ~icode[2], ~icode[1], icode[3]);  // AND_Gate
  or or_1 (NeedValC, and_1_out, and_2_out, and_3_out, and_4_out, and_5_out);

  // Notes on the sheet:
  //   irmovq (3)
  //   rmmovq (4)
  //   mrmovq (5)
  //   jXX (7)
  //   call (8)
endmodule

module Need_Regids (
  input  [3:0] icode,
  output NeedRegids
);

  wire and_1_out, and_2_out, and_3_out, and_4_out, and_5_out, and_6_out, and_7_out;

  and and_1 (and_1_out, ~icode[0], icode[1], ~icode[2], ~icode[3]);  // AND_Gate
  and and_2 (and_2_out, icode[0], icode[1], ~icode[2], ~icode[3]);  // AND_Gate
  and and_3 (and_3_out, ~icode[0], ~icode[1], icode[2], ~icode[3]);  // AND_Gate
  and and_4 (and_4_out, icode[0], ~icode[1], icode[2], ~icode[3]);  // AND_Gate
  and and_5 (and_5_out, ~icode[0], icode[1], icode[2], ~icode[3]);  // AND_Gate
  and and_6 (and_6_out, ~icode[0], icode[1], ~icode[2], icode[3]);  // AND_Gate
  and and_7 (and_7_out, icode[0], icode[1], ~icode[2], icode[3]);  // AND_Gate
  or or_1 (NeedRegids, and_1_out, and_2_out, and_3_out, and_4_out, and_5_out, and_6_out, and_7_out);

  // Notes on the sheet:
  //   rrmovq (2)
  //   irmovq (3)
  //   rmmovq (4)
  //   mrmovq (5)
  //   OPq (6)
  //   pushq (a)
  //   popq (b)
endmodule

module Align (
  input  [7:0] Byte1,
  input  [7:0] Byte2,
  input  [7:0] Byte3,
  input  [7:0] Byte4,
  input  [7:0] Byte5,
  input  [7:0] Byte6,
  input  [7:0] Byte7,
  input  [7:0] Byte8,
  input  [7:0] Byte9,
  input  NeedRegids,
  output [3:0] rA,
  output [3:0] rB,
  output [63:0] valC
);

  Multiplexer #(.width(8)) multiplexer_1 (.in0({8{1'b1}}), .in1(Byte1), .out({rA, rB}), .sel(NeedRegids));
  Multiplexer #(.width(8)) multiplexer_2 (.in0(Byte1), .in1(Byte2), .out(valC[7:0]), .sel(NeedRegids));
  Multiplexer #(.width(8)) multiplexer_3 (.in0(Byte2), .in1(Byte3), .out(valC[15:8]), .sel(NeedRegids));
  Multiplexer #(.width(8)) multiplexer_4 (.in0(Byte3), .in1(Byte4), .out(valC[23:16]), .sel(NeedRegids));
  Multiplexer #(.width(8)) multiplexer_5 (.in0(Byte4), .in1(Byte5), .out(valC[31:24]), .sel(NeedRegids));
  Multiplexer #(.width(8)) multiplexer_6 (.in0(Byte5), .in1(Byte6), .out(valC[39:32]), .sel(NeedRegids));
  Multiplexer #(.width(8)) multiplexer_7 (.in0(Byte6), .in1(Byte7), .out(valC[47:40]), .sel(NeedRegids));
  Multiplexer #(.width(8)) multiplexer_8 (.in0(Byte7), .in1(Byte8), .out(valC[55:48]), .sel(NeedRegids));
  Multiplexer #(.width(8)) multiplexer_9 (.in0(Byte8), .in1(Byte9), .out(valC[63:56]), .sel(NeedRegids));

  // Notes on the sheet:
  //   rA and rB set to 0xf if not needed
endmodule

module RegisterFile (
  input  [63:0] valE,
  input  [63:0] valM,
  input  [3:0] dstE,
  input  [3:0] dstM,
  input  [3:0] srcA,
  input  [3:0] srcB,
  input  clk,
  input  write_en,
  input  read_en,
  output [63:0] valA,
  output [63:0] valB,
  output [63:0] val_rax,
  output [63:0] val_rcx,
  output [63:0] val_rdx,
  output [63:0] val_rbx,
  output [63:0] val_rsp,
  output [63:0] val_rbp,
  output [63:0] val_rsi,
  output [63:0] val_rdi,
  output [63:0] val_r8,
  output [63:0] val_r9,
  output [63:0] val_r10,
  output [63:0] val_r11,
  output [63:0] val_r12,
  output [63:0] val_r13,
  output [63:0] val_r14
);

  wire and_1_out, decoder_1_out0, decoder_1_out1, decoder_1_out2, decoder_1_out3, decoder_1_out4,
       decoder_1_out5, decoder_1_out6, decoder_1_out7, decoder_1_out8, decoder_1_out9, decoder_1_out10,
       decoder_1_out11, decoder_1_out12, decoder_1_out13, decoder_1_out14, decoder_2_out0, decoder_2_out1,
       decoder_2_out2, decoder_2_out3, decoder_2_out4, decoder_2_out5, decoder_2_out6, decoder_2_out7,
       decoder_2_out8, decoder_2_out9, decoder_2_out10, decoder_2_out11, decoder_2_out12, decoder_2_out13,
       decoder_2_out14, or_1_out, or_2_out, or_3_out, or_4_out, or_5_out, or_6_out, or_7_out, or_8_out,
       or_9_out, or_10_out, or_11_out, or_12_out, or_13_out, or_14_out, or_15_out, or_16_out;
  wire [63:0] multiplexer_1_out, multiplexer_2_out, multiplexer_3_out, multiplexer_4_out, multiplexer_5_out,
       multiplexer_6_out, multiplexer_7_out, multiplexer_8_out, multiplexer_9_out, multiplexer_10_out,
       multiplexer_11_out, multiplexer_12_out, multiplexer_13_out, multiplexer_14_out, multiplexer_15_out,
       multiplexer_16_out, multiplexer_17_out;

  Decoder #(.select(4)) decoder_1 (
    .out0(decoder_1_out0), .out1(decoder_1_out1), .out2(decoder_1_out2), .out3(decoder_1_out3),
    .out4(decoder_1_out4), .out5(decoder_1_out5), .out6(decoder_1_out6), .out7(decoder_1_out7),
    .out8(decoder_1_out8), .out9(decoder_1_out9), .out10(decoder_1_out10), .out11(decoder_1_out11),
    .out12(decoder_1_out12), .out13(decoder_1_out13), .out14(decoder_1_out14), .sel(dstE), .en(write_en));  // open: out15
  Decoder #(.select(4)) decoder_2 (
    .out0(decoder_2_out0), .out1(decoder_2_out1), .out2(decoder_2_out2), .out3(decoder_2_out3),
    .out4(decoder_2_out4), .out5(decoder_2_out5), .out6(decoder_2_out6), .out7(decoder_2_out7),
    .out8(decoder_2_out8), .out9(decoder_2_out9), .out10(decoder_2_out10), .out11(decoder_2_out11),
    .out12(decoder_2_out12), .out13(decoder_2_out13), .out14(decoder_2_out14), .sel(dstM), .en(write_en));  // open: out15
  or or_1 (or_1_out, write_en, read_en);
  and and_1 (and_1_out, or_1_out, clk);
  or or_2 (or_2_out, decoder_1_out0, decoder_2_out0);
  or or_3 (or_3_out, decoder_1_out1, decoder_2_out1);
  or or_4 (or_4_out, decoder_1_out2, decoder_2_out2);
  or or_5 (or_5_out, decoder_1_out3, decoder_2_out3);
  or or_6 (or_6_out, decoder_1_out4, decoder_2_out4);
  or or_7 (or_7_out, decoder_1_out5, decoder_2_out5);
  or or_8 (or_8_out, decoder_1_out6, decoder_2_out6);
  or or_9 (or_9_out, decoder_1_out7, decoder_2_out7);
  or or_10 (or_10_out, decoder_1_out8, decoder_2_out8);
  or or_11 (or_11_out, decoder_1_out9, decoder_2_out9);
  or or_12 (or_12_out, decoder_1_out10, decoder_2_out10);
  or or_13 (or_13_out, decoder_1_out11, decoder_2_out11);
  or or_14 (or_14_out, decoder_1_out12, decoder_2_out12);
  or or_15 (or_15_out, decoder_1_out13, decoder_2_out13);
  or or_16 (or_16_out, decoder_1_out14, decoder_2_out14);
  Multiplexer #(.width(64)) multiplexer_1 (.in0(valM), .in1(valE), .out(multiplexer_1_out), .sel(decoder_1_out14));
  Multiplexer #(.width(64)) multiplexer_2 (.in0(valM), .in1(valE), .out(multiplexer_2_out), .sel(decoder_1_out0));
  Multiplexer #(.width(64)) multiplexer_3 (.in0(valM), .in1(valE), .out(multiplexer_3_out), .sel(decoder_1_out1));
  Multiplexer #(.width(64)) multiplexer_4 (.in0(valM), .in1(valE), .out(multiplexer_4_out), .sel(decoder_1_out2));
  Multiplexer #(.width(64)) multiplexer_5 (.in0(valM), .in1(valE), .out(multiplexer_5_out), .sel(decoder_1_out3));
  Multiplexer #(.width(64)) multiplexer_6 (.in0(valM), .in1(valE), .out(multiplexer_6_out), .sel(decoder_1_out4));
  Multiplexer #(.width(64)) multiplexer_7 (.in0(valM), .in1(valE), .out(multiplexer_7_out), .sel(decoder_1_out5));
  Multiplexer #(.width(64)) multiplexer_8 (.in0(valM), .in1(valE), .out(multiplexer_8_out), .sel(decoder_1_out6));
  Multiplexer #(.width(64)) multiplexer_9 (.in0(valM), .in1(valE), .out(multiplexer_9_out), .sel(decoder_1_out7));
  Multiplexer #(.width(64)) multiplexer_10 (.in0(valM), .in1(valE), .out(multiplexer_10_out), .sel(decoder_1_out8));
  Multiplexer #(.width(64)) multiplexer_11 (.in0(valM), .in1(valE), .out(multiplexer_11_out), .sel(decoder_1_out9));
  Multiplexer #(.width(64)) multiplexer_12 (.in0(valM), .in1(valE), .out(multiplexer_12_out), .sel(decoder_1_out10));
  Multiplexer #(.width(64)) multiplexer_13 (.in0(valM), .in1(valE), .out(multiplexer_13_out), .sel(decoder_1_out11));
  Multiplexer #(.width(64)) multiplexer_14 (.in0(valM), .in1(valE), .out(multiplexer_14_out), .sel(decoder_1_out12));
  Multiplexer #(.width(64)) multiplexer_15 (.in0(valM), .in1(valE), .out(multiplexer_15_out), .sel(decoder_1_out13));
  Register #(.width(64)) rax (.D(multiplexer_2_out), .en(or_2_out), .clk(and_1_out), .Q(val_rax));  // open: clr
  Register #(.width(64)) rcx (.D(multiplexer_3_out), .en(or_3_out), .clk(and_1_out), .Q(val_rcx));  // open: clr
  Register #(.width(64)) rdx (.D(multiplexer_4_out), .en(or_4_out), .clk(and_1_out), .Q(val_rdx));  // open: clr
  Register #(.width(64)) rbx (.D(multiplexer_5_out), .en(or_5_out), .clk(and_1_out), .Q(val_rbx));  // open: clr
  Register #(.width(64)) rsp (.D(multiplexer_6_out), .en(or_6_out), .clk(and_1_out), .Q(val_rsp));  // open: clr
  Register #(.width(64)) rbp (.D(multiplexer_7_out), .en(or_7_out), .clk(and_1_out), .Q(val_rbp));  // open: clr
  Register #(.width(64)) rsi (.D(multiplexer_8_out), .en(or_8_out), .clk(and_1_out), .Q(val_rsi));  // open: clr
  Register #(.width(64)) rdi (.D(multiplexer_9_out), .en(or_9_out), .clk(and_1_out), .Q(val_rdi));  // open: clr
  Register #(.width(64)) r8 (.D(multiplexer_10_out), .en(or_10_out), .clk(and_1_out), .Q(val_r8));  // open: clr
  Register #(.width(64)) r9 (.D(multiplexer_11_out), .en(or_11_out), .clk(and_1_out), .Q(val_r9));  // open: clr
  Register #(.width(64)) r10 (.D(multiplexer_12_out), .en(or_12_out), .clk(and_1_out), .Q(val_r10));  // open: clr
  Register #(.width(64)) r11 (.D(multiplexer_13_out), .en(or_13_out), .clk(and_1_out), .Q(val_r11));  // open: clr
  Register #(.width(64)) r12 (.D(multiplexer_14_out), .en(or_14_out), .clk(and_1_out), .Q(val_r12));  // open: clr
  Register #(.width(64)) r13 (.D(multiplexer_15_out), .en(or_15_out), .clk(and_1_out), .Q(val_r13));  // open: clr
  Register #(.width(64)) r14 (.D(multiplexer_1_out), .en(or_16_out), .clk(and_1_out), .Q(val_r14));  // open: clr
  Multiplexer #(.enable("true"), .select(4), .width(64)) multiplexer_16 (
    .in0(val_rax), .in1(val_rcx), .in2(val_rdx), .in3(val_rbx), .in4(val_rsp), .in5(val_rbp), .in6(val_rsi),
    .in7(val_rdi), .in8(val_r8), .in9(val_r9), .in10(val_r10), .in11(val_r11), .in12(val_r12),
    .in13(val_r13), .in14(val_r14), .out(multiplexer_16_out), .sel(srcA), .en(read_en));  // open: in15
  Multiplexer #(.enable("true"), .select(4), .width(64)) multiplexer_17 (
    .in0(val_rax), .in1(val_rcx), .in2(val_rdx), .in3(val_rbx), .in4(val_rsp), .in5(val_rbp), .in6(val_rsi),
    .in7(val_rdi), .in8(val_r8), .in9(val_r9), .in10(val_r10), .in11(val_r11), .in12(val_r12),
    .in13(val_r13), .in14(val_r14), .out(multiplexer_17_out), .sel(srcB), .en(read_en));  // open: in15
  Register #(.width(64)) register_1 (.D(multiplexer_16_out), .en(read_en), .clk(and_1_out), .Q(valA));  // open: clr
  Register #(.width(64)) register_2 (.D(multiplexer_17_out), .en(read_en), .clk(and_1_out), .Q(valB));  // open: clr
endmodule

module srcA (
  input  [3:0] icode,
  input  [3:0] rA,
  output [3:0] src_A
);

  wire call_out, Opq_out, or_1_out, or_2_out, popq_out, pushq_out, ret_out, rmmovq_out, rrmovq_out;
  wire [3:0] multiplexer_1_out;

  and rrmovq (rrmovq_out, ~icode[3], ~icode[2], icode[1], ~icode[0]);  // AND_Gate
  and rmmovq (rmmovq_out, ~icode[3], icode[2], ~icode[1], ~icode[0]);  // AND_Gate
  and Opq (Opq_out, ~icode[3], icode[2], icode[1], ~icode[0]);  // AND_Gate
  and pushq (pushq_out, icode[3], ~icode[2], icode[1], ~icode[0]);  // AND_Gate
  and call (call_out, icode[3], ~icode[2], ~icode[1], ~icode[0]);  // AND_Gate
  and ret (ret_out, icode[3], ~icode[2], ~icode[1], icode[0]);  // AND_Gate
  and popq (popq_out, icode[3], ~icode[2], icode[1], icode[0]);  // AND_Gate
  or or_1 (or_1_out, rrmovq_out, rmmovq_out, Opq_out, pushq_out);
  or or_2 (or_2_out, call_out, ret_out, popq_out);
  Multiplexer #(.width(4)) multiplexer_1 (.in0(4'b1111), .in1(4'b0100), .out(multiplexer_1_out), .sel(or_2_out));
  Multiplexer #(.width(4)) multiplexer_2 (.in0(multiplexer_1_out), .in1(rA), .out(src_A), .sel(or_1_out));
endmodule

module srcB (
  input  [3:0] icode,
  input  [3:0] rB,
  output [3:0] src_B
);

  wire call_out, mrmovq_out, Opq_out, or_1_out, or_2_out, popq_out, pushq_out, ret_out, rmmovq_out,
       rrmovq_out;
  wire [3:0] multiplexer_1_out;

  and call (call_out, icode[3], ~icode[2], ~icode[1], ~icode[0]);  // AND_Gate
  and ret (ret_out, icode[3], ~icode[2], ~icode[1], icode[0]);  // AND_Gate
  and popq (popq_out, icode[3], ~icode[2], icode[1], icode[0]);  // AND_Gate
  and pushq (pushq_out, icode[3], ~icode[2], icode[1], ~icode[0]);  // AND_Gate
  and rrmovq (rrmovq_out, ~icode[3], ~icode[2], icode[1], ~icode[0]);  // AND_Gate
  and rmmovq (rmmovq_out, ~icode[3], icode[2], ~icode[1], ~icode[0]);  // AND_Gate
  and Opq (Opq_out, ~icode[3], icode[2], icode[1], ~icode[0]);  // AND_Gate
  and mrmovq (mrmovq_out, ~icode[3], icode[2], ~icode[1], icode[0]);  // AND_Gate
  or or_1 (or_1_out, call_out, ret_out, popq_out, pushq_out);
  or or_2 (or_2_out, rrmovq_out, rmmovq_out, Opq_out, mrmovq_out);
  Multiplexer #(.width(4)) multiplexer_1 (.in0(4'b1111), .in1(4'b0100), .out(multiplexer_1_out), .sel(or_1_out));
  Multiplexer #(.width(4)) multiplexer_2 (.in0(multiplexer_1_out), .in1(rB), .out(src_B), .sel(or_2_out));
endmodule

module dstM (
  input  [3:0] icode,
  input  [3:0] rA,
  input  WB,
  output [3:0] dst_M
);

  wire and_1_out, call_out, mr_out, not_1_out, OP_out, or_1_out, or_2_out, or_3_out, pop_out, push_out,
       ret_out, rm_out, rr_out;
  wire [3:0] controlled_buffer_1_out, controlled_buffer_4_out;

  and rr (rr_out, ~icode[3], ~icode[2], icode[1], ~icode[0]);  // AND_Gate
  and rm (rm_out, ~icode[3], icode[2], ~icode[1], ~icode[0]);  // AND_Gate
  and OP (OP_out, ~icode[3], icode[2], icode[1], ~icode[0]);  // AND_Gate
  and push (push_out, icode[3], ~icode[2], icode[1], ~icode[0]);  // AND_Gate
  and call (call_out, icode[3], ~icode[2], ~icode[1], ~icode[0]);  // AND_Gate
  and ret (ret_out, icode[3], ~icode[2], ~icode[1], icode[0]);  // AND_Gate
  and pop (pop_out, icode[3], ~icode[2], icode[1], icode[0]);  // AND_Gate
  and mr (mr_out, ~icode[3], icode[2], ~icode[1], icode[0]);  // AND_Gate
  or or_1 (or_1_out, rr_out, rm_out, OP_out, push_out);
  or or_2 (or_2_out, call_out, ret_out, pop_out);
  and and_1 (and_1_out, ~or_1_out, ~or_2_out);  // AND_Gate
  or or_3 (or_3_out, mr_out, pop_out);
  not not_1 (not_1_out, or_3_out);
  assign controlled_buffer_1_out = or_1_out ? rA : 4'bz;  // Controlled_Buffer controlled_buffer_1
  assign controlled_buffer_1_out = or_2_out ? 4'b0100 : 4'bz;  // Controlled_Buffer controlled_buffer_2
  assign controlled_buffer_1_out = and_1_out ? 4'b1111 : 4'bz;  // Controlled_Buffer controlled_buffer_3
  assign controlled_buffer_4_out = or_3_out ? rA : 4'bz;  // Controlled_Buffer controlled_buffer_4
  assign controlled_buffer_4_out = not_1_out ? 4'b1111 : 4'bz;  // Controlled_Buffer controlled_buffer_5
  Multiplexer #(.width(4)) multiplexer_1 (
    .in0(controlled_buffer_1_out), .in1(controlled_buffer_4_out), .out(dst_M), .sel(WB));

  // Notes on the sheet:
  //   Decode
  //   Decode:
  //   Write back
  //   %rsp: call, ret, popq
  //   rA
  //   %rsp
  //   N/A
  //   rA
  //   N/A
  //   rA: rrmovq, rmmovq, OPq, pushq
  //   Write back:
  //   rA: mrmovq, popq
  //   %rsp: none
endmodule

module dstE (
  input  [3:0] icode,
  input  [3:0] rB,
  input  WB,
  output [3:0] dst_E
);

  wire and_1_out, and_2_out, call_out, ir_out, mr_out, opq_out, or_1_out, or_2_out, or_3_out, popq_out,
       pushq_out, ret_out, rm_out, rr_out;
  wire [3:0] controlled_buffer_1_out, controlled_buffer_4_out;

  and rr (rr_out, ~icode[3], ~icode[2], icode[1], ~icode[0]);  // AND_Gate
  and rm (rm_out, ~icode[3], icode[2], ~icode[1], ~icode[0]);  // AND_Gate
  and mr (mr_out, ~icode[3], icode[2], ~icode[1], icode[0]);  // AND_Gate
  and opq (opq_out, ~icode[3], icode[2], icode[1], ~icode[0]);  // AND_Gate
  and call (call_out, icode[3], ~icode[2], ~icode[1], ~icode[0]);  // AND_Gate
  and ret (ret_out, icode[3], ~icode[2], ~icode[1], icode[0]);  // AND_Gate
  and pushq (pushq_out, icode[3], ~icode[2], icode[1], ~icode[0]);  // AND_Gate
  and popq (popq_out, icode[3], ~icode[2], icode[1], icode[0]);  // AND_Gate
  and ir (ir_out, ~icode[3], ~icode[2], icode[1], icode[0]);  // AND_Gate
  or or_1 (or_1_out, rr_out, rm_out, mr_out, opq_out);
  or or_2 (or_2_out, call_out, ret_out, pushq_out, popq_out);
  and and_1 (and_1_out, ~or_1_out, ~or_2_out);  // AND_Gate
  or or_3 (or_3_out, rr_out, ir_out, opq_out);
  and and_2 (and_2_out, ~or_3_out, ~or_2_out);  // AND_Gate
  assign controlled_buffer_1_out = or_1_out ? rB : 4'bz;  // Controlled_Buffer controlled_buffer_1
  assign controlled_buffer_1_out = or_2_out ? 4'b0100 : 4'bz;  // Controlled_Buffer controlled_buffer_2
  assign controlled_buffer_1_out = and_1_out ? 4'b1111 : 4'bz;  // Controlled_Buffer controlled_buffer_3
  assign controlled_buffer_4_out = or_3_out ? rB : 4'bz;  // Controlled_Buffer controlled_buffer_4
  assign controlled_buffer_4_out = or_2_out ? 4'b0100 : 4'bz;  // Controlled_Buffer controlled_buffer_5
  assign controlled_buffer_4_out = and_2_out ? 4'b1111 : 4'bz;  // Controlled_Buffer controlled_buffer_6
  Multiplexer #(.width(4)) multiplexer_1 (
    .in0(controlled_buffer_1_out), .in1(controlled_buffer_4_out), .out(dst_E), .sel(WB));

  // Notes on the sheet:
  //   Decode:
  //   Decode
  //   Write Back
  //   %rsp: call, ret, pushq, popq
  //   rB
  //   %rsp
  //   N/A
  //   rB
  //   %rsp
  //   N/A
  //   rB: rrmovq, rmmovq, mrmovq, OPq
  //   %rsp is the same
  //   Write back:
  //   rB: rrmovq, irmovq, OPq, 
  //   %rsp: call, ret, pushq, popq
endmodule

module ALU (
  input  [63:0] A,
  input  [63:0] B,
  input  [1:0] fn,
  output [63:0] valE,
  output [63:0] pA,
  output [63:0] pB
);

  wire and_2_out;
  wire [63:0] and_1_out, not_1_out, xor_1_out;

  assign not_1_out = ~A;  // NOT_Gate not_1, 64 bits wide
  assign and_1_out = A & B;  // AND_Gate and_1, 64 bits wide
  assign xor_1_out = A ^ B;  // XOR_Gate xor_1, 64 bits wide
  and and_2 (and_2_out, fn[0], ~fn[1]);  // AND_Gate
  Multiplexer #(.select(2), .width(64)) multiplexer_1 (
    .in0(A), .in1(not_1_out), .in2(and_1_out), .in3(xor_1_out), .out(pA), .sel(fn));
  Multiplexer #(.select(2), .width(64)) multiplexer_2 (
    .in0(B), .in1(B), .in2({64{1'b0}}), .in3({64{1'b0}}), .out(pB), .sel(fn));
  Adder #(.width(64)) adder_1 (.a(pA), .b(pB), .out(valE), .cin(and_2_out));  // open: cout

  // Notes on the sheet:
  //   A - B
  //   0 0 ADD
  //   0 1 SUB
  //   1 0 AND
  //   1 1 XOR
endmodule

module ALU_A (
  input  [63:0] valA,
  input  [63:0] valC,
  input  [3:0] icode,
  output [63:0] A
);

  wire [1:0] rom_1_data;

  ROM #(.addrWidth(4), .dataWidth(2)) rom_1 (.addr(icode), .data(rom_1_data));
  Multiplexer #(.select(2), .width(64)) multiplexer_1 (
    .in0(64'hfffffffffffffff8), .in1(64'h8), .in2(valA), .in3(valC), .out(A), .sel(rom_1_data));

  // Notes on the sheet:
  //   contents of rom_1 (hex, n*v repeats v):
  //   0 0 2 3 3 3 2 0 0 1 0 1
  //   used ROM to select from mux based on instruction
  //   Can be -8, 8, valA, or valC
  //   Shouldn't matter what is used for jXX, halt, and nop
endmodule

module ALU_B (
  input  [63:0] valB,
  input  [3:0] icode,
  output [63:0] B
);

  wire undriven;

  ROM #(.addrWidth(4), .dataWidth(1)) rom_1 (.addr(icode));  // open: data
  Multiplexer #(.width(64)) multiplexer_1 (.in0({64{1'b0}}), .in1(valB), .out(B), .sel(undriven));

  // Notes on the sheet:
  //   contents of rom_1 (hex, n*v repeats v):
  //   4*0 1 1 1 0 4*1
  //   used ROM to select from mux based on instruction
  //   Can be valB or 0
  //   Shouldn't matter what is used for jXX, halt, and nop
endmodule

module ALU_fun (
  input  [3:0] ifun,
  input  [3:0] icode,
  output [1:0] fn
);

  wire and_1_out;

  and and_1 (and_1_out, ~icode[0], icode[1], icode[2], ~icode[3]);  // AND_Gate
  Multiplexer #(.width(2)) multiplexer_1 (.in0(2'b00), .in1(ifun[1:0]), .out(fn), .sel(and_1_out));

  // Notes on the sheet:
  //   Use ADD unless OPq
  //   Shouldn't matter what is used for jXX, halt, and nop
  //   OPq
  //   0 0 ADD
  //   0 1 SUB
  //   1 0 AND
  //   1 1 XOR
endmodule

module SetCC (
  input  [3:0] icode,
  output set
);

  and and_1 (set, ~icode[0], icode[1], icode[2], ~icode[3]);  // AND_Gate

  // Notes on the sheet:
  //   OPq
endmodule

module CC (
  input  SetCC,
  input  [63:0] valE,
  input  [63:0] A,
  input  [63:0] B,
  input  clk,
  input  en,
  output [2:0] code
);

  wire and_1_out, comparator_3_lt, comparator_4_lt, comparator_5_lt, comparator_6_eq, comparator_7_eq;
  wire [2:0] comparator_1_eq;

  and and_1 (and_1_out, clk, en);
  Comparator #(.width(64)) comparator_1 (.a(valE), .b({64{1'b0}}), .eq(comparator_1_eq[0]));  // open: gt, lt
  Comparator #(.width(64)) comparator_2 (.a(valE), .b({64{1'b0}}), .lt(comparator_1_eq[1]));  // open: gt, eq
  Comparator #(.width(64)) comparator_3 (.a(A), .b({64{1'b0}}), .lt(comparator_3_lt));  // open: gt, eq
  Comparator #(.width(64)) comparator_4 (.a(B), .b({64{1'b0}}), .lt(comparator_4_lt));  // open: gt, eq
  Comparator #(.width(64)) comparator_5 (.a(valE), .b({64{1'b0}}), .lt(comparator_5_lt));  // open: gt, eq
  Comparator #(.width(1)) comparator_6 (
    .a(comparator_3_lt), .b(comparator_4_lt), .eq(comparator_6_eq));  // open: gt, lt
  Comparator #(.width(1)) comparator_7 (
    .a(comparator_3_lt), .b(comparator_5_lt), .eq(comparator_7_eq));  // open: gt, lt
  and and_2 (comparator_1_eq[2], comparator_6_eq, ~comparator_7_eq);  // AND_Gate
  Register #(.width(3)) register_1 (.D(comparator_1_eq), .en(SetCC), .clk(and_1_out), .Q(code));  // open: clr

  // Notes on the sheet:
  //   ZF: t == 0
  //   SF: t < 0
  //   OF: (a < 0 == b < 0) && (t < 0 != a < 0)
  //   Bit 0 - ZF
  //   Bit 1 - SF
  //   Bit 2 - OF
endmodule

module cond (
  input  [2:0] code,
  input  [3:0] ifun,
  output Cnd
);

  wire and_1_out, and_2_out, and_3_out, and_4_out, and_5_out, and_6_out, and_7_out, decoder_1_out0,
       decoder_1_out1, decoder_1_out2, decoder_1_out3, decoder_1_out4, decoder_1_out5, decoder_1_out6,
       or_1_out, xor_1_out;

  Decoder #(.enable("false"), .select(3)) decoder_1 (
    .out0(decoder_1_out0), .out1(decoder_1_out1), .out2(decoder_1_out2), .out3(decoder_1_out3),
    .out4(decoder_1_out4), .out5(decoder_1_out5), .out6(decoder_1_out6), .sel(ifun[2:0]));  // open: out7
  xor xor_1 (xor_1_out, code[1], code[2]);
  or or_1 (or_1_out, xor_1_out, code[0]);
  and and_1 (and_1_out, ~xor_1_out, ~code[0]);  // AND_Gate
  and and_2 (and_2_out, or_1_out, decoder_1_out1);
  and and_3 (and_3_out, xor_1_out, decoder_1_out2);
  and and_4 (and_4_out, code[0], decoder_1_out3);
  and and_5 (and_5_out, ~code[0], decoder_1_out4);  // AND_Gate
  and and_6 (and_6_out, ~xor_1_out, decoder_1_out5);  // AND_Gate
  and and_7 (and_7_out, and_1_out, decoder_1_out6);
  or or_2 (Cnd, decoder_1_out0, and_2_out, and_3_out, and_4_out, and_5_out, and_6_out, and_7_out);

  // Notes on the sheet:
  //   OF
  //   SF
  //   jmp: 1
  //   jle: (SF ^ OF) | ZF
  //   jl: SF ^ OF
  //   je: ZF
  //   jne: ~ZF
  //   jge: ~(SF ^ OF)
  //   ZF
  //   jg: ~(SF ^ OF) & ~ZF
endmodule

module DataMemory (
  input  mwrite,
  input  mread,
  input  [11:0] mAddress,
  input  [63:0] mData,
  input  en,
  input  clk,
  output [63:0] valM
);

  wire and_1_out, and_2_out, counter_1_q, decoder_1_out0, decoder_1_out1, decoder_1_out2, decoder_1_out3,
       decoder_1_out4, decoder_1_out5, decoder_1_out6, decoder_1_out7, not_1_out;
  wire [2:0] counter_2_q;
  wire [7:0] multiplexer_1_out, ram_1_dout;
  wire [11:0] adder_1_out;

  not not_1 (not_1_out, en);
  Counter #(.max('h1), .ongoal("stay"), .width(1)) counter_1 (
    .clk(clk), .Q(counter_1_q));  // open: clr, load, up, count, D, carry
  and and_1 (and_1_out, mread, en);
  and and_2 (and_2_out, mwrite, en);
  Counter #(.max('h7), .width(3)) counter_2 (
    .clr(not_1_out), .count(counter_1_q), .clk(clk), .Q(counter_2_q));  // open: load, up, D, carry
  Adder #(.width(12)) adder_1 (.a(mAddress), .b({{9{1'b0}}, counter_2_q}), .out(adder_1_out));  // open: cin, cout
  Multiplexer #(.select(3), .width(8)) multiplexer_1 (
    .in0(mData[7:0]), .in1(mData[15:8]), .in2(mData[23:16]), .in3(mData[31:24]), .in4(mData[39:32]),
    .in5(mData[47:40]), .in6(mData[55:48]), .in7(mData[63:56]), .out(multiplexer_1_out), .sel(counter_2_q));
  RAM #(.addrWidth(12)) ram_1 (
    .addr(adder_1_out), .we(and_2_out), .oe(mread), .clk(clk), .din(multiplexer_1_out), .dout(ram_1_dout));
  Decoder #(.select(3)) decoder_1 (
    .out0(decoder_1_out0), .out1(decoder_1_out1), .out2(decoder_1_out2), .out3(decoder_1_out3),
    .out4(decoder_1_out4), .out5(decoder_1_out5), .out6(decoder_1_out6), .out7(decoder_1_out7),
    .sel(counter_2_q), .en(and_1_out));
  Register register_1 (.D(ram_1_dout), .en(decoder_1_out1), .clk(clk), .Q(valM[7:0]));  // open: clr
  Register register_2 (.D(ram_1_dout), .en(decoder_1_out2), .clk(clk), .Q(valM[15:8]));  // open: clr
  Register register_3 (.D(ram_1_dout), .en(decoder_1_out3), .clk(clk), .Q(valM[23:16]));  // open: clr
  Register register_4 (.D(ram_1_dout), .en(decoder_1_out4), .clk(clk), .Q(valM[31:24]));  // open: clr
  Register register_5 (.D(ram_1_dout), .en(decoder_1_out5), .clk(clk), .Q(valM[39:32]));  // open: clr
  Register register_6 (.D(ram_1_dout), .en(decoder_1_out6), .clk(clk), .Q(valM[47:40]));  // open: clr
  Register register_7 (.D(ram_1_dout), .en(decoder_1_out7), .clk(clk), .Q(valM[55:48]));  // open: clr
  Register register_8 (.D(ram_1_dout), .en(decoder_1_out0), .clk(clk), .Q(valM[63:56]));  // open: clr

  // Notes on the sheet:
  //   don't want to increment counter until second clock tick
  //   and the first register ends up being the last value
  //   RAM needs a clock signal to read each value and each register needs a clock signal
  //   these can't happen at the same time, so two additional clock signals are needed and
endmodule

module MemData (
  input  [3:0] icode,
  input  [63:0] valA,
  input  [11:0] valP,
  output [63:0] DataIn
);

  wire call_out, or_1_out, push_out, rm_out, xor_1_out;
  wire [63:0] multiplexer_1_out;

  and rm (rm_out, ~icode[3], icode[2], ~icode[1], ~icode[0]);  // AND_Gate
  and push (push_out, icode[3], ~icode[2], icode[1], ~icode[0]);  // AND_Gate
  and call (call_out, icode[3], ~icode[2], ~icode[1], ~icode[0]);  // AND_Gate
  or or_1 (or_1_out, rm_out, push_out);
  Multiplexer #(.width(64)) multiplexer_1 (
    .in0(valA), .in1({{52{1'b0}}, valP}), .out(multiplexer_1_out), .sel(call_out));
  xor xor_1 (xor_1_out, or_1_out, call_out);
  Multiplexer #(.width(64)) multiplexer_2 (.in1(multiplexer_1_out), .out(DataIn), .sel(xor_1_out));  // open: in0
endmodule

module MemAddr (
  input  [3:0] icode,
  input  [63:0] valE,
  input  [63:0] valA,
  output [11:0] AddrIn
);

  wire call_out, mr_out, or_1_out, or_2_out, pop_out, push_out, ret_out, rm_out, xor_1_out;
  wire [11:0] multiplexer_1_out;

  and rm (rm_out, ~icode[3], icode[2], ~icode[1], ~icode[0]);  // AND_Gate
  and push (push_out, icode[3], ~icode[2], icode[1], ~icode[0]);  // AND_Gate
  and call (call_out, icode[3], ~icode[2], ~icode[1], ~icode[0]);  // AND_Gate
  and mr (mr_out, ~icode[3], icode[2], ~icode[1], icode[0]);  // AND_Gate
  and pop (pop_out, icode[3], ~icode[2], icode[1], icode[0]);  // AND_Gate
  and ret (ret_out, icode[3], ~icode[2], ~icode[1], icode[0]);  // AND_Gate
  or or_1 (or_1_out, rm_out, push_out, call_out, mr_out);
  or or_2 (or_2_out, pop_out, ret_out);
  Multiplexer #(.width(12)) multiplexer_1 (.in0(valE[11:0]), .in1(valA[11:0]), .out(multiplexer_1_out), .sel(or_2_out));
  xor xor_1 (xor_1_out, or_1_out, or_2_out);
  Multiplexer #(.width(12)) multiplexer_2 (.in1(multiplexer_1_out), .out(AddrIn), .sel(xor_1_out));  // open: in0
endmodule

module MemWrite (
  input  [3:0] icode,
  output WriteE
);

  wire call_out, push_out, rm_out;

  and rm (rm_out, ~icode[3], icode[2], ~icode[1], ~icode[0]);  // AND_Gate
  and push (push_out, icode[3], ~icode[2], icode[1], ~icode[0]);  // AND_Gate
  and call (call_out, icode[3], ~icode[2], ~icode[1], ~icode[0]);  // AND_Gate
  or or_1 (WriteE, rm_out, push_out, call_out);
endmodule

module MemRead (
  input  [3:0] icode,
  output ReadE
);

  wire mr_out, pop_out, ret_out;

  and mr (mr_out, ~icode[3], icode[2], ~icode[1], icode[0]);  // AND_Gate
  and ret (ret_out, icode[3], ~icode[2], ~icode[1], icode[0]);  // AND_Gate
  and pop (pop_out, icode[3], ~icode[2], icode[1], icode[0]);  // AND_Gate
  or or_1 (ReadE, mr_out, ret_out, pop_out);
endmodule

module WriteBack (
  input  [3:0] icode,
  input  [1:0] ifun,
  input  [63:0] valM,
  input  [63:0] valE,
  output [2:0] addr_rB_rsp_rA,
  output [63:0] valM_out,
  output [63:0] valE_out
);

  wire or_1_out, read_ra_1_rb, read_ra_1_rsp, read_ra_1_valid, read_ra_1_valm_ra;
  wire [63:0] controlled_buffer_4_out, controlled_buffer_5_out;

  read_rA read_ra_1 (
    .icode(icode), .ifun(ifun), .valM_rA(read_ra_1_valm_ra), .valid(read_ra_1_valid), .rsp(read_ra_1_rsp),
    .rB(read_ra_1_rb));
  assign addr_rB_rsp_rA[0] = read_ra_1_valid ? read_ra_1_valm_ra : 1'bz;  // Controlled_Buffer controlled_buffer_1
  assign addr_rB_rsp_rA[1] = read_ra_1_valid ? read_ra_1_rsp : 1'bz;  // Controlled_Buffer controlled_buffer_2
  assign addr_rB_rsp_rA[2] = read_ra_1_valid ? read_ra_1_rb : 1'bz;  // Controlled_Buffer controlled_buffer_3
  assign controlled_buffer_4_out = read_ra_1_valid ? valM : 64'bz;  // Controlled_Buffer controlled_buffer_4
  assign controlled_buffer_5_out = read_ra_1_valid ? valE : 64'bz;  // Controlled_Buffer controlled_buffer_5
  assign valM_out = addr_rB_rsp_rA[0] ? controlled_buffer_4_out : 64'bz;  // Controlled_Buffer controlled_buffer_6
  or or_1 (or_1_out, addr_rB_rsp_rA[1], addr_rB_rsp_rA[2]);
  assign valE_out = or_1_out ? controlled_buffer_5_out : 64'bz;  // Controlled_Buffer controlled_buffer_7
endmodule

module read_rA (
  input  [3:0] icode,
  input  [1:0] ifun,
  output valM_rA,
  output valid,
  output rsp,
  output rB
);

  wire call_out, ir_out, mr_out, op_out, or_1_out, or_2_out, or_3_out, or_6_out, popq_out, pushq_out,
       ret_out, rr_out;

  or or_1 (or_1_out, ifun[0], ifun[1]);
  or or_2 (or_2_out, ifun[0], ifun[1]);
  and rr (rr_out, ~icode[3], ~icode[2], icode[1], ~icode[0], ~or_1_out);  // AND_Gate
  and ir (ir_out, ~icode[3], ~icode[2], icode[1], icode[0]);  // AND_Gate
  and mr (mr_out, ~icode[3], icode[2], ~icode[1], icode[0]);  // AND_Gate
  and op (op_out, ~icode[3], icode[2], icode[1], ~icode[0]);  // AND_Gate
  and call (call_out, icode[3], ~icode[2], ~icode[1], ~icode[0]);  // AND_Gate
  and ret (ret_out, icode[3], ~icode[2], ~icode[1], icode[0]);  // AND_Gate
  and pushq (pushq_out, icode[3], ~icode[2], icode[1], ~icode[0]);  // AND_Gate
  and popq (popq_out, icode[3], ~icode[2], icode[1], icode[0]);  // AND_Gate
  and cmove (rB, ~icode[3], ~icode[2], icode[1], ~icode[0], or_2_out);  // AND_Gate
  or or_3 (or_3_out, rr_out, ir_out, mr_out, op_out);
  or or_4 (rsp, call_out, ret_out, pushq_out, popq_out);
  or or_5 (valid, or_3_out, or_6_out);
  or or_6 (or_6_out, rB, rsp);
  or or_7 (valM_rA, or_3_out, popq_out);
endmodule

module UpdateUnit (
  input  [3:0] icode,
  input  Cnd,
  input  [11:0] valP,
  input  [63:0] valC,
  input  [63:0] valM,
  input  PCU,
  input  clk,
  output [11:0] PC
);

  wire and_1_out, and_2_out, call_out, ir_out, jXX_out, mr_out, nop_out, op_out, or_1_out, or_2_out,
       or_3_out, popq_out, pushq_out, ret_out, rm_out, rr_out;
  wire [11:0] controlled_buffer_1_out;

  and rr (rr_out, ~icode[3], ~icode[2], icode[1], ~icode[0]);  // AND_Gate
  and ir (ir_out, ~icode[3], ~icode[2], icode[1], icode[0]);  // AND_Gate
  and rm (rm_out, ~icode[3], icode[2], ~icode[1], ~icode[0]);  // AND_Gate
  and mr (mr_out, ~icode[3], icode[2], ~icode[1], icode[0]);  // AND_Gate
  and op (op_out, ~icode[3], icode[2], icode[1], ~icode[0]);  // AND_Gate
  and pushq (pushq_out, icode[3], ~icode[2], icode[1], ~icode[0]);  // AND_Gate
  and popq (popq_out, icode[3], ~icode[2], icode[1], icode[0]);  // AND_Gate
  and nop (nop_out, ~icode[3], ~icode[2], ~icode[1], icode[0]);  // AND_Gate
  and jXX (jXX_out, ~icode[3], icode[2], icode[1], icode[0]);  // AND_Gate
  and call (call_out, icode[3], ~icode[2], ~icode[1], ~icode[0]);  // AND_Gate
  and ret (ret_out, icode[3], ~icode[2], ~icode[1], icode[0]);  // AND_Gate
  and and_1 (and_1_out, ~Cnd, jXX_out);  // AND_Gate
  and and_2 (and_2_out, Cnd, jXX_out);
  or or_1 (or_1_out, rr_out, ir_out, rm_out, mr_out, op_out, pushq_out, popq_out, nop_out);
  or or_2 (or_2_out, or_1_out, and_1_out);
  or or_3 (or_3_out, and_2_out, call_out);
  assign controlled_buffer_1_out = or_2_out ? valP : 12'bz;  // Controlled_Buffer controlled_buffer_1
  assign controlled_buffer_1_out = or_3_out ? valC[11:0] : 12'bz;  // Controlled_Buffer controlled_buffer_2
  assign controlled_buffer_1_out = ret_out ? valM[11:0] : 12'bz;  // Controlled_Buffer controlled_buffer_3
  Register #(.width(12)) register_1 (.D(controlled_buffer_1_out), .en(PCU), .clk(clk), .Q(PC));  // open: clr

  // Notes on the sheet:
  //   PC <-- valP
  //   PC <-- valC
  //   PC <-- valM
  //   PC <-- Cnd ? valC : valP
  //   use valP
  //   use valC
  //   use valM
endmodule

module GlobalCounter (
  input  clk,
  input  HLT,
  output [15:0] instr_count,
  output FET,
  output DEC,
  output EXE,
  output MEM,
  output WB,
  output PCU
);

  wire comparator_4_gt, comparator_5_lt, comparator_8_eq, counter_1_q, not_1_out;
  wire [4:0] counter_2_q, multiplexer_1_out;

  Counter #(.max('h1), .ongoal("stay"), .width(1)) counter_1 (
    .clk(clk), .Q(counter_1_q));  // open: clr, load, up, count, D, carry
  Counter #(.max('h17), .width(5)) counter_2 (
    .count(counter_1_q), .clk(clk), .Q(counter_2_q));  // open: clr, load, up, D, carry
  not not_1 (not_1_out, HLT);
  Multiplexer #(.width(5)) multiplexer_1 (.in0(counter_2_q), .in1({5{1'b0}}), .out(multiplexer_1_out), .sel(HLT));
  Comparator #(.mode("unsigned"), .width(5)) comparator_1 (
    .a(multiplexer_1_out), .b(5'b01010), .lt(FET));  // open: gt, eq
  Comparator #(.mode("unsigned"), .width(5)) comparator_2 (
    .a(multiplexer_1_out), .b(5'b01010), .eq(DEC));  // open: gt, lt
  Comparator #(.mode("unsigned"), .width(5)) comparator_3 (
    .a(multiplexer_1_out), .b(5'b01011), .eq(EXE));  // open: gt, lt
  Comparator #(.mode("unsigned"), .width(5)) comparator_4 (
    .a(multiplexer_1_out), .b(5'b01011), .gt(comparator_4_gt));  // open: eq, lt
  Comparator #(.mode("unsigned"), .width(5)) comparator_5 (
    .a(multiplexer_1_out), .b(5'b10110), .lt(comparator_5_lt));  // open: gt, eq
  Comparator #(.mode("unsigned"), .width(5)) comparator_6 (
    .a(multiplexer_1_out), .b(5'b10110), .eq(WB));  // open: gt, lt
  Comparator #(.mode("unsigned"), .width(5)) comparator_7 (
    .a(multiplexer_1_out), .b(5'b10111), .eq(PCU));  // open: gt, lt
  Comparator #(.mode("unsigned"), .width(5)) comparator_8 (
    .a(counter_2_q), .b({5{1'b0}}), .eq(comparator_8_eq));  // open: gt, lt
  and and_1 (MEM, comparator_4_gt, comparator_5_lt);
  Counter #(.max('hffff), .width(16)) counter_3 (
    .count(not_1_out), .clk(comparator_8_eq), .Q(instr_count));  // open: clr, load, up, D, carry

  // Notes on the sheet:
  //   don't want to start counting until second clock tick
  //   instruction start
  //   pins indicate which phase we are in based on clock cycle
  //   number of instructions completed
endmodule
